# Fritzing sketch Wiring Diagram (saved by Fritzing 0.9.3b)
circuit board: 8.46667cm x 5.64444cm
breadboards: 1

parts:
  Part1 = Arduino Pro Mini v13
  U1 = 2.4" TFT LCD screen, SPI, Touch-enabled
  U2 = ESP8266 WiFi Module [part_number=ESP8266]
  Part2 = FTDI Basic Programmer
  RHT1 = Humidity and Temperature Sensor RHT03

nets:
  N1: Part1.DTR, Part2.DTR
  N2: Part1.D0/TX, Part2.RXI
  N3: Part1.D1/RX, Part2.TXO
  VCC: Part1.VCC, U1.LED, U1.RESET, U1.VCC, U2.VCC, U2.CH_PD, Part2.POWER, RHT1.Vcc
  GND: Part1.GND, Part1.RAW, U1.GND, U2.GND, Part2.CTS, Part2.GND, RHT1.GND_1
  N4: Part1.A1, RHT1.Data-signal
  N5: Part1.A0, Part1.D13/SCK, U1.SCL
  N6: Part1.D12/MISO, U1.SDO
  N7: Part1.D11_PWM/MOSI, U1.SDA
  N8: Part1.D10_PWM/SS, U1.CS
  N9: Part1.D9_PWM, U1.DC
  N10: Part1.D8, U2.TXD
  N11: Part1.D7, U1.T_IRQ
  N12: Part1.D6_PWM, U1.T_DO
  N13: Part1.D5_PWM, U1.T_DIN
  N14: Part1.D4, U1.T_CS
  N15: Part1.D3_PWM, U1.T_CLK
  N16: Part1.D2, U2.RXD

custom parts:
  2.4" TFT LCD screen, SPI, Touch-enabled: 2.4", ILI9341-based TFT LCD screen with touch-sensing using the XPT2046 controller, SPI-compatible. There is also an SD-card version that is non-touch enabled but uses exactly the same board and pinout. This part is for both, though it should be noted that the SD reader and the touch screen are mutually incompatible
  ESP8266 WiFi Module: Generic WiFi Module based on the ESP8266 with onboard PCB antenna and UART communications
